// Logisim project contador_senha.circ as structural Verilog: 1 circuit, main circuit main
module main (
  input  [2:0] s,
  output cont_end
);

  wire and_1_out, and_2_out, clock_out, j_k_ff_1_q, j_k_ff_2_q, not_1_out, not_2_out, not_3_out, or_1_out;

  Clock clock (.out(clock_out));
  not not_1 (not_1_out, s[0]);
  and and_1 (and_1_out, not_1_out, s[1], not_2_out);
  not not_2 (not_2_out, s[2]);
  and and_2 (and_2_out, s[0], s[1], not_3_out);
  not not_3 (not_3_out, s[2]);
  or or_1 (or_1_out, and_1_out, and_2_out);
  J_K_Flip_Flop #(.NegatePresetClear("true")) j_k_ff_1 (
    .J(1'b1), .clk(clock_out), .K(1'b1), .Q(j_k_ff_1_q), .preset(1'b1), .reset(or_1_out));  // open: Qn
  J_K_Flip_Flop #(.NegatePresetClear("true")) j_k_ff_2 (
    .J(j_k_ff_1_q), .clk(clock_out), .K(j_k_ff_1_q), .Q(j_k_ff_2_q), .preset(1'b1), .reset(or_1_out));  // open: Qn
  and and_3 (cont_end, j_k_ff_2_q, j_k_ff_1_q);
endmodule
