// Logisim project contador_cres_decres.circ as structural Verilog: 1 circuit, main circuit main
module main (
  input  up_dw,
  input  clr
);

  wire and_1_out, and_2_out, and_3_out, and_4_out, clock_out, JK_1, JK_2, not_1_out, not_2_out, not_3_out,
       not_4_out, Q_0, Q_1;
  wire [2:2] j_k_ff_3_q;

  not not_1 (not_1_out, up_dw);
  Clock clock (.out(clock_out));
  not not_2 (not_2_out, Q_0);
  not not_3 (not_3_out, Q_1);
  and and_1 (and_1_out, up_dw, Q_0, Q_1);
  or or_1 (JK_2, and_1_out, and_2_out);
  and and_2 (and_2_out, not_2_out, not_3_out, not_1_out);
  and and_3 (and_3_out, up_dw, Q_0);
  not not_4 (not_4_out, Q_0);
  and and_4 (and_4_out, not_4_out, not_1_out);
  J_K_Flip_Flop #(.NegatePresetClear("true")) j_k_ff_1 (
    .J(1'b1), .clk(clock_out), .K(1'b1), .Q(Q_0), .preset(1'b1), .reset(clr));  // open: Qn
  or or_2 (JK_1, and_3_out, and_4_out);
  J_K_Flip_Flop #(.NegatePresetClear("true")) j_k_ff_2 (
    .J(JK_1), .clk(clock_out), .K(JK_1), .Q(Q_1), .preset(1'b1), .reset(clr));  // open: Qn
  J_K_Flip_Flop #(.NegatePresetClear("true")) j_k_ff_3 (
    .J(JK_2), .clk(clock_out), .K(JK_2), .Q(j_k_ff_3_q[2]), .preset(1'b1), .reset(clr));  // open: Qn
  Decoder #(.select(3), .enable("false")) decoder_1 (.sel({j_k_ff_3_q[2], Q_1, Q_0}));  // open: out0, out1, out2, out3, out4, out5, out6, out7
endmodule
