// Logisim project regi_min.circ as structural Verilog: 1 circuit, main circuit main
module main (
  input  clr,
  input  [11:0] A_reg,
  input  mx_mi,
  input  load,
  output [11:0] A_min
);

  wire and_1_out, not_1_out;
  wire [11:0] multiplexer_1_out;

  not not_1 (not_1_out, mx_mi);
  and and_1 (and_1_out, not_1_out, load);
  Multiplexer #(.width(12)) multiplexer_1 (.in0(A_reg), .in1({12{1'b0}}), .out(multiplexer_1_out), .sel(clr));
  Multiplexer #(.width(12)) multiplexer_2 (.in0({12{1'b0}}), .in1(multiplexer_1_out), .out(A_min), .sel(and_1_out));
endmodule
