// Logisim project regi_passo.circ as structural Verilog: 1 circuit, main circuit main
module main (
  input  clr,
  input  [3:0] A_0,
  input  step,
  input  load,
  output [3:0] passo
);

  wire and_1_out;
  wire [3:0] multiplexer_1_out, multiplexer_2_out;

  and and_1 (and_1_out, step, load);
  Multiplexer #(.width(4)) multiplexer_1 (.in0(4'b0000), .in1(4'b0001), .out(multiplexer_1_out), .sel(clr));
  Multiplexer #(.width(4)) multiplexer_2 (.in0(A_0), .in1(multiplexer_1_out), .out(multiplexer_2_out), .sel(clr));
  Multiplexer #(.width(4)) multiplexer_3 (.in0(4'b0000), .in1(multiplexer_2_out), .out(passo), .sel(and_1_out));
endmodule
